// Logisim project flip_flop_counters.circ as structural Verilog: 4 circuits, main circuit Zad1D
module Zad1D (
);

  wire and_1_out, clock_1_out, d_ff_1_qn, d_ff_2_qn, d_ff_3_qn, q0_qn;
  wire [3:0] q0_q;

  Clock clock_1 (.out(clock_1_out));
  D_Flip_Flop q0 (.D(q0_qn), .clk(clock_1_out), .Q(q0_q[0]), .Qn(q0_qn), .reset(and_1_out));  // open: preset
  D_Flip_Flop d_ff_1 (.D(d_ff_1_qn), .clk(q0_qn), .Q(q0_q[1]), .Qn(d_ff_1_qn), .reset(and_1_out));  // open: preset
  and and_1 (and_1_out, q0_q[1], q0_q[3]);
  D_Flip_Flop d_ff_2 (.D(d_ff_2_qn), .clk(d_ff_1_qn), .Q(q0_q[2]), .Qn(d_ff_2_qn), .reset(and_1_out));  // open: preset
  D_Flip_Flop d_ff_3 (.D(d_ff_3_qn), .clk(d_ff_2_qn), .Q(q0_q[3]), .Qn(d_ff_3_qn), .reset(and_1_out));  // open: preset
  Hex_Digit_Display hex_digit_display_1 (.value(q0_q));  // open: dp
endmodule

module Zad1T (
);

  wire and_1_out, and_2_out, and_3_out, clock_1_out;
  wire [3:0] q0_q;

  Clock clock_1 (.out(clock_1_out));
  Hex_Digit_Display #(.decimalPoint("false")) hex_digit_display_1 (.value(q0_q));
  T_Flip_Flop q0 (.T(1'b1), .clk(clock_1_out), .Q(q0_q[0]), .reset(and_2_out));  // open: Qn, preset
  T_Flip_Flop q1 (.T(q0_q[0]), .clk(clock_1_out), .Q(q0_q[1]), .reset(and_2_out));  // open: Qn, preset
  and and_1 (and_1_out, q0_q[0], q0_q[1]);
  and and_2 (and_2_out, q0_q[1], q0_q[3]);
  T_Flip_Flop q2 (.T(and_1_out), .clk(clock_1_out), .Q(q0_q[2]), .reset(and_2_out));  // open: Qn, preset
  and and_3 (and_3_out, q0_q[0], q0_q[1], q0_q[2]);
  T_Flip_Flop q3 (.T(and_3_out), .clk(clock_1_out), .Q(q0_q[3]), .reset(and_2_out));  // open: Qn, preset
endmodule

module Zad2 (
  output [3:0] paralell_out,
  output serial_out
);

  wire clock_1_out, Reset_out;

  Clock clock_1 (.out(clock_1_out));
  D_Flip_Flop d_ff_1 (.D(1'b1), .clk(clock_1_out), .Q(paralell_out[3]), .reset(Reset_out));  // open: Qn, preset
  D_Flip_Flop d_ff_2 (
    .D(paralell_out[3]), .clk(clock_1_out), .Q(paralell_out[2]), .reset(Reset_out));  // open: Qn, preset
  D_Flip_Flop d_ff_3 (
    .D(paralell_out[2]), .clk(clock_1_out), .Q(paralell_out[1]), .reset(Reset_out));  // open: Qn, preset
  D_Flip_Flop d_ff_4 (
    .D(paralell_out[1]), .clk(clock_1_out), .Q(paralell_out[0]), .reset(Reset_out));  // open: Qn, preset
  Button Reset (.out(Reset_out));

  assign serial_out = paralell_out[0];
endmodule

module zad3 (
  input  in_1,
  input  in_2,
  input  in_3,
  input  in_4,
  output [3:0] out_5
);

  wire clock_1_out, Reset_out;

  Clock clock_1 (.out(clock_1_out));
  D_Flip_Flop d_ff_1 (.D(in_1), .clk(clock_1_out), .Q(out_5[0]), .reset(Reset_out));  // open: Qn, preset
  D_Flip_Flop d_ff_2 (.D(in_2), .clk(clock_1_out), .Q(out_5[1]), .reset(Reset_out));  // open: Qn, preset
  D_Flip_Flop d_ff_3 (.D(in_3), .clk(clock_1_out), .Q(out_5[2]), .reset(Reset_out));  // open: Qn, preset
  D_Flip_Flop d_ff_4 (.D(in_4), .clk(clock_1_out), .Q(out_5[3]), .reset(Reset_out));  // open: Qn, preset
  Button Reset (.out(Reset_out));
endmodule
