// Logisim project flip_flop_registers.circ as structural Verilog: 2 circuits, main circuit rejestr_rownolegly
module rejestr_rownolegly (
  input  read_lock,
  input  clk,
  input  save_lock,
  input  [3:0] save,
  input  clear,
  output [3:0] read
);

  wire and_1_out, d_ff_1_q, d_ff_2_q, d_ff_3_q, d_ff_4_q;

  and and_1 (and_1_out, clk, save_lock);
  D_Flip_Flop d_ff_1 (.D(save[0]), .clk(and_1_out), .Q(d_ff_1_q), .reset(clear));  // open: Qn, preset
  D_Flip_Flop d_ff_2 (.D(save[1]), .clk(and_1_out), .Q(d_ff_2_q), .reset(clear));  // open: Qn, preset
  D_Flip_Flop d_ff_3 (.D(save[2]), .clk(and_1_out), .Q(d_ff_3_q), .reset(clear));  // open: Qn, preset
  D_Flip_Flop d_ff_4 (.D(save[3]), .clk(and_1_out), .Q(d_ff_4_q), .reset(clear));  // open: Qn, preset
  and and_2 (read[0], d_ff_1_q, read_lock);
  and and_3 (read[1], d_ff_2_q, read_lock);
  and and_4 (read[2], d_ff_3_q, read_lock);
  and and_5 (read[3], d_ff_4_q, read_lock);
endmodule

module zadanie (
  input  write_lock,
  input  [3:0] write_data,
  input  [1:0] write_reg,
  input  [1:0] read_reg1,
  input  lock_read,
  input  [1:0] read_reg2,
  output [3:0] read_data1,
  output [3:0] read_data2
);

  wire clck_out, clear_registers_out;
  wire [3:0] demultiplexer_1_out0, demultiplexer_1_out1, demultiplexer_1_out2, demultiplexer_1_out3,
       Reg0_read, Reg1_read, Reg2_read;

  Demultiplexer #(.disabled("Z"), .select(2), .width(4)) demultiplexer_1 (
    .out0(demultiplexer_1_out0), .out1(demultiplexer_1_out1), .out2(demultiplexer_1_out2),
    .out3(demultiplexer_1_out3), .in(write_data), .sel(write_reg));
  Button clear_registers (.out(clear_registers_out));
  Clock clck (.out(clck_out));
  rejestr_rownolegly Reg0 (
    .read_lock(lock_read), .clk(clck_out), .save_lock(write_lock), .save(demultiplexer_1_out0),
    .clear(clear_registers_out), .read(Reg0_read));
  rejestr_rownolegly Reg1 (
    .read_lock(lock_read), .clk(clck_out), .save_lock(write_lock), .save(demultiplexer_1_out1),
    .clear(clear_registers_out), .read(Reg1_read));
  rejestr_rownolegly Reg2 (
    .read_lock(lock_read), .clk(clck_out), .save_lock(write_lock), .save(demultiplexer_1_out2),
    .clear(clear_registers_out), .read(Reg2_read));
  rejestr_rownolegly Reg3 (
    .read_lock(lock_read), .clk(clck_out), .save_lock(write_lock), .save(demultiplexer_1_out3),
    .clear(clear_registers_out), .read(Reg2_read));
  Multiplexer #(.select(2), .width(4)) multiplexer_1 (
    .in0(Reg0_read), .in1(Reg1_read), .in2(Reg2_read), .in3(Reg2_read), .out(read_data1), .sel(read_reg1));
  Multiplexer #(.select(2), .width(4)) multiplexer_2 (
    .in0(Reg0_read), .in1(Reg1_read), .in2(Reg2_read), .in3(Reg2_read), .out(read_data2), .sel(read_reg2));

  // Notes on the sheet:
  //   aby moc zapisac, write_lock musi byc wlaczony, tak samo zeby odczytac lock_read musi byc wlaczony
endmodule
