// Logisim project logical_gates.circ as structural Verilog: 6 circuits, main circuit Koniunkcja
module Koniunkcja (
  input  in_1,
  input  in_2,
  output out_3
);

  wire nand_1_out;

  nand nand_1 (nand_1_out, in_1, in_2);
  nand nand_2 (out_3, nand_1_out, nand_1_out);
endmodule

module Alternatywa (
  input  in_1,
  input  in_2,
  output out_3
);

  wire nand_1_out, nand_2_out;

  nand nand_1 (nand_1_out, in_1, in_1);
  nand nand_2 (nand_2_out, in_2, in_2);
  nand nand_3 (out_3, nand_1_out, nand_2_out);
endmodule

module Zaprzeczenie (
  input  in_1,
  output out_2
);

  nand nand_1 (out_2, in_1, in_1);
endmodule

module Implikacja (
  input  in_1,
  input  in_2,
  output out_3
);

  wire nand_1_out;

  nand nand_1 (nand_1_out, in_2, in_2);
  nand nand_2 (out_3, in_1, nand_1_out);
endmodule

module suma_eski (
  input  X0,
  input  X1,
  input  X2,
  input  X4,
  output out_5
);

  wire Y1_out, Y2_out, Y3_out, Y7_out, Y9_out;

  and Y2 (Y2_out, ~X0, X1, ~X2, ~X4);  // AND_Gate
  and Y3 (Y3_out, X0, X1, ~X2, ~X4);  // AND_Gate
  and Y7 (Y7_out, X0, X1, X2, ~X4);  // AND_Gate
  and Y1 (Y1_out, X0, ~X1, ~X2, ~X4);  // AND_Gate
  and Y9 (Y9_out, X0, ~X1, ~X2, X4);  // AND_Gate
  or or_1 (out_5, Y2_out, Y3_out, Y7_out, Y1_out, Y9_out);

  // Notes on the sheet:
  //   S23719 = 2 3 7 1 9
endmodule

module suma_eski_7400 (
  input  X1,
  input  X2,
  input  X3,
  input  X4,
  output out_5
);

  wire n7400_1_pin3, n7400_2_pin3, n7400_2_pin6, n7400_2_pin11, n7400_3_pin3, n7400_3_pin11, n7400_4_pin3,
       n7400_4_pin6, n7400_4_pin11, n7400_5_pin3, n7400_5_pin6, n7400_6_pin3, n7400_6_pin6, n7400_6_pin8,
       n7400_6_pin11, n7400_7_pin3, n7400_7_pin6, n7400_7_pin8, n7400_7_pin11, n7400_8_pin3, n7400_8_pin6,
       n7400_8_pin8, n7400_8_pin11, n7400_9_pin3, n7400_9_pin6, n7400_9_pin8, n7400_9_pin11, n7400_10_pin3,
       n7400_10_pin6, n7400_10_pin8, n7400_10_pin11, n7400_11_pin8, n7400_11_pin11, n7400_12_pin8,
       n7400_12_pin11, n7400_13_pin8, n7400_13_pin11, n7400_14_pin8, n7400_14_pin11, n7400_15_pin8,
       n7400_15_pin11, n7400_16_pin4, n7400_16_pin5, n7400_16_pin6, n7400_17_pin4, n7400_17_pin5,
       n7400_17_pin6, n7400_18_pin4, n7400_18_pin5, n7400_18_pin6, n7400_19_pin4, n7400_19_pin5;

  _7400 u_7400_1 (
    .pin1(X4), .pin2(X4), .pin3(n7400_1_pin3));  // open: pin4, pin5, pin6, pin13, pin12, pin11, pin10, pin9, pin8
  _7400 u_7400_2 (
    .pin1(X3), .pin2(X3), .pin3(n7400_2_pin3), .pin4(X4), .pin5(X4), .pin6(n7400_2_pin6), .pin13(X2),
    .pin12(X2), .pin11(n7400_2_pin11));  // open: pin10, pin9, pin8
  _7400 u_7400_3 (
    .pin1(X3), .pin2(X3), .pin3(n7400_3_pin3), .pin13(X2), .pin12(X2), .pin11(n7400_3_pin11));  // open: pin4, pin5, pin6, pin10, pin9, pin8
  _7400 u_7400_4 (
    .pin1(X3), .pin2(X3), .pin3(n7400_4_pin3), .pin4(X4), .pin5(X4), .pin6(n7400_4_pin6), .pin13(X1),
    .pin12(X1), .pin11(n7400_4_pin11));  // open: pin10, pin9, pin8
  _7400 u_7400_5 (
    .pin1(X3), .pin2(X3), .pin3(n7400_5_pin3), .pin4(X4), .pin5(X4), .pin6(n7400_5_pin6));  // open: pin13, pin12, pin11, pin10, pin9, pin8
  _7400 u_7400_6 (
    .pin1(n7400_4_pin3), .pin2(n7400_4_pin6), .pin3(n7400_6_pin3), .pin4(n7400_6_pin3), .pin5(n7400_6_pin3),
    .pin6(n7400_6_pin6), .pin13(n7400_4_pin11), .pin12(X2), .pin11(n7400_6_pin11), .pin10(n7400_6_pin11),
    .pin9(n7400_6_pin11), .pin8(n7400_6_pin8));
  _7400 u_7400_7 (
    .pin1(n7400_5_pin3), .pin2(n7400_5_pin6), .pin3(n7400_7_pin3), .pin4(n7400_7_pin3), .pin5(n7400_7_pin3),
    .pin6(n7400_7_pin6), .pin13(X2), .pin12(X1), .pin11(n7400_7_pin11), .pin10(n7400_7_pin11),
    .pin9(n7400_7_pin11), .pin8(n7400_7_pin8));
  _7400 u_7400_8 (
    .pin1(n7400_1_pin3), .pin2(X3), .pin3(n7400_8_pin3), .pin4(n7400_8_pin3), .pin5(n7400_8_pin3),
    .pin6(n7400_8_pin6), .pin13(X2), .pin12(X1), .pin11(n7400_8_pin11), .pin10(n7400_8_pin11),
    .pin9(n7400_8_pin11), .pin8(n7400_8_pin8));
  _7400 u_7400_9 (
    .pin1(n7400_2_pin3), .pin2(n7400_2_pin6), .pin3(n7400_9_pin3), .pin4(n7400_9_pin3), .pin5(n7400_9_pin3),
    .pin6(n7400_9_pin6), .pin13(n7400_2_pin11), .pin12(X1), .pin11(n7400_9_pin11), .pin10(n7400_9_pin11),
    .pin9(n7400_9_pin11), .pin8(n7400_9_pin8));
  _7400 u_7400_10 (
    .pin1(n7400_3_pin3), .pin2(X4), .pin3(n7400_10_pin3), .pin4(n7400_10_pin3), .pin5(n7400_10_pin3),
    .pin6(n7400_10_pin6), .pin13(n7400_3_pin11), .pin12(X1), .pin11(n7400_10_pin11), .pin10(n7400_10_pin11),
    .pin9(n7400_10_pin11), .pin8(n7400_10_pin8));
  _7400 u_7400_11 (
    .pin13(n7400_6_pin6), .pin12(n7400_6_pin8), .pin11(n7400_11_pin11), .pin10(n7400_11_pin11),
    .pin9(n7400_11_pin11), .pin8(n7400_11_pin8));  // open: pin1, pin2, pin3, pin4, pin5, pin6
  _7400 u_7400_12 (
    .pin13(n7400_7_pin6), .pin12(n7400_7_pin8), .pin11(n7400_12_pin11), .pin10(n7400_12_pin11),
    .pin9(n7400_12_pin11), .pin8(n7400_12_pin8));  // open: pin1, pin2, pin3, pin4, pin5, pin6
  _7400 u_7400_13 (
    .pin13(n7400_8_pin6), .pin12(n7400_8_pin8), .pin11(n7400_13_pin11), .pin10(n7400_13_pin11),
    .pin9(n7400_13_pin11), .pin8(n7400_13_pin8));  // open: pin1, pin2, pin3, pin4, pin5, pin6
  _7400 u_7400_14 (
    .pin13(n7400_9_pin6), .pin12(n7400_9_pin8), .pin11(n7400_14_pin11), .pin10(n7400_14_pin11),
    .pin9(n7400_14_pin11), .pin8(n7400_14_pin8));  // open: pin1, pin2, pin3, pin4, pin5, pin6
  _7400 u_7400_15 (
    .pin13(n7400_10_pin6), .pin12(n7400_10_pin8), .pin11(n7400_15_pin11), .pin10(n7400_15_pin11),
    .pin9(n7400_15_pin11), .pin8(n7400_15_pin8));  // open: pin1, pin2, pin3, pin4, pin5, pin6
  _7400 u_7400_16 (
    .pin4(n7400_16_pin4), .pin5(n7400_16_pin5), .pin6(n7400_16_pin6), .pin13(n7400_14_pin8),
    .pin12(n7400_14_pin8), .pin11(n7400_16_pin5), .pin10(n7400_15_pin8), .pin9(n7400_15_pin8),
    .pin8(n7400_16_pin4));  // open: pin1, pin2, pin3
  _7400 u_7400_17 (
    .pin4(n7400_17_pin4), .pin5(n7400_17_pin5), .pin6(n7400_17_pin6), .pin13(n7400_11_pin8),
    .pin12(n7400_11_pin8), .pin11(n7400_17_pin5), .pin10(n7400_12_pin8), .pin9(n7400_12_pin8),
    .pin8(n7400_17_pin4));  // open: pin1, pin2, pin3
  _7400 u_7400_18 (
    .pin4(n7400_18_pin4), .pin5(n7400_18_pin5), .pin6(n7400_18_pin6), .pin13(n7400_16_pin6),
    .pin12(n7400_16_pin6), .pin11(n7400_18_pin5), .pin10(n7400_13_pin8), .pin9(n7400_13_pin8),
    .pin8(n7400_18_pin4));  // open: pin1, pin2, pin3
  _7400 u_7400_19 (
    .pin4(n7400_19_pin4), .pin5(n7400_19_pin5), .pin6(out_5), .pin13(n7400_18_pin6), .pin12(n7400_18_pin6),
    .pin11(n7400_19_pin4), .pin10(n7400_17_pin6), .pin9(n7400_17_pin6), .pin8(n7400_19_pin5));  // open: pin1, pin2, pin3

  // Notes on the sheet:
  //   Y2
  //   Y3
  //   Y1
  //   Y9
  //   Y7
  //   AND
  //   AND
  //   AND
  //   AND
  //   AND
  //   OR
  //   OR
  //   OR
  //   OR
endmodule
