// Logisim project logical_operations.circ as structural Verilog: 1 circuit, main circuit zadanie_1_2
module zadanie_1_2 (
  input  in_1,
  input  in_2,
  input  in_3,
  input  in_4,
  output out_5
);

  wire and_1_out, and_2_out, and_3_out;

  and and_1 (and_1_out, ~in_3, ~in_2, in_1);  // AND_Gate
  and and_2 (and_2_out, ~in_4, ~in_3, in_2);  // AND_Gate
  and and_3 (and_3_out, ~in_4, in_2, in_1);  // AND_Gate
  or or_1 (out_5, and_1_out, and_2_out, and_3_out);

  // Notes on the sheet:
  //   S23719
  //   Wzor: y = ~x2*~x1*x0 + ~x3*~x2*x1 + ~x3*x1*x0 
endmodule
