// Logisim project multiplexers.circ as structural Verilog: 2 circuits, main circuit Zad1
module Zad1 (
  input  x2,
  input  x3,
  input  x0,
  input  x1,
  output out_5
);

  wire nor_1_out;

  nor nor_1 (nor_1_out, x2, x3);
  Multiplexer #(.select(2)) multiplexer_1 (
    .in0(1'b0), .in1(1'b1), .in2(nor_1_out), .in3(1'b1), .out(out_5), .sel({x1, x0}));
endmodule

module Zad2 (
  input  [3:0] Input1,
  input  [3:0] Input2,
  input  [3:0] OpCode,
  output [3:0] out_4
);

  wire [3:0] adder_1_out, and_1_out, nand_1_out, not_1_out, not_2_out, or_1_out, subtractor_1_out, xor_1_out;

  Adder #(.width(4)) adder_1 (.a(Input1), .b(Input2), .out(adder_1_out));  // open: cin, cout
  Subtractor #(.width(4)) subtractor_1 (.a(Input1), .b(Input2), .out(subtractor_1_out));  // open: bin, bout
  assign and_1_out = Input1 & Input2;  // AND_Gate and_1, 4 bits wide
  assign or_1_out = Input1 | Input2;  // OR_Gate or_1, 4 bits wide
  assign nand_1_out = ~(Input1 & Input2);  // NAND_Gate nand_1, 4 bits wide
  assign xor_1_out = Input1 ^ Input2;  // XOR_Gate xor_1, 4 bits wide
  assign not_1_out = ~Input1;  // NOT_Gate not_1, 4 bits wide
  assign not_2_out = ~Input2;  // NOT_Gate not_2, 4 bits wide
  Multiplexer #(.select(4), .width(4)) multiplexer_1 (
    .in4(adder_1_out), .in5(subtractor_1_out), .in6(and_1_out), .in7(or_1_out), .in8(nand_1_out),
    .in9(xor_1_out), .in10(not_1_out), .in11(not_1_out), .in12(not_2_out), .out(out_4), .sel(OpCode));  // open: in0, in1, in2, in3, in13, in14, in15

  // Notes on the sheet:
  //   Wybor operacji
endmodule
